// Logisim project d_ff.circ as structural Verilog: 1 circuit, main circuit d_ff
module d_ff (
  input  d,
  input  clk,
  output q
);

  wire m, m_nd, m_r, m_s, mn, nc, qn, s_nd, s_r, s_s;

  not u_nc (nc, clk);
  nand u_m_s (m_s, d, nc);
  nand u_m_nd (m_nd, d, d);
  nand u_m_r (m_r, m_nd, nc);
  nand u_m (m, m_s, mn);
  nand u_mn (mn, m_r, m);
  nand u_s_s (s_s, m, clk);
  nand u_s_nd (s_nd, m, m);
  nand u_s_r (s_r, s_nd, clk);
  nand u_q (q, s_s, qn);
  nand u_qn (qn, s_r, q);
endmodule
