// Logisim project d_ff_async.circ as structural Verilog: 1 circuit, main circuit d_ff_async
module d_ff_async (
  input  d,
  input  clk,
  input  set,
  input  clr,
  output q
);

  wire busy, crn, es, m, m_dr, m_ds, m_enable, m_nd, m_r, m_s, mn, nc, qn, run, s_dr, s_ds, s_enable, s_nd,
       s_r, s_s;

  not u_nc (nc, clk);
  not u_crn (crn, clr);
  or u_busy (busy, set, clr);
  not u_run (run, busy);
  and u_es (es, set, crn);
  not u_m_nd (m_nd, d);
  and u_m_enable (m_enable, nc, run);
  and u_m_ds (m_ds, d, m_enable);
  and u_m_dr (m_dr, m_nd, m_enable);
  or u_m_s (m_s, m_ds, es);
  or u_m_r (m_r, m_dr, clr);
  nor u_m (m, m_r, mn);
  nor u_mn (mn, m_s, m);
  not u_s_nd (s_nd, m);
  and u_s_enable (s_enable, clk, run);
  and u_s_ds (s_ds, m, s_enable);
  and u_s_dr (s_dr, s_nd, s_enable);
  or u_s_s (s_s, s_ds, es);
  or u_s_r (s_r, s_dr, clr);
  nor u_q (q, s_r, qn);
  nor u_qn (qn, s_s, q);
endmodule
