// Logisim project d_latch.circ as structural Verilog: 1 circuit, main circuit d_latch
module d_latch (
  input  d,
  input  en,
  output q
);

  wire l_nd, l_r, l_s, qn;

  nand u_l_s (l_s, d, en);
  nand u_l_nd (l_nd, d, d);
  nand u_l_r (l_r, l_nd, en);
  nand u_q (q, l_s, qn);
  nand u_qn (qn, l_r, q);
endmodule
