// Logisim project rs_latch.circ as structural Verilog: 1 circuit, main circuit rs_latch
module rs_latch (
  input  s,
  input  r,
  output q,
  output qn
);

  nor u_q (q, r, qn);
  nor u_qn (qn, s, q);
endmodule
